# Fritzing sketch BTS7960 Connection System (saved by Fritzing 0.9.3b)
stripboards: 5
perfboards: 3

parts:
  M1 = BTS7960 [part_number=BTS7960(IC0)]
  M2 = BTS7960 [part_number=BTS7960(IC1)]
  M3 = BTS7960 [part_number=BTS7960(IC3)]
  M4 = BTS7960 [part_number=BTS7960(IC2)]
  U1 = 4053 [part_number=74HC4053(IC0) package="DIP (Dual Inline) [THT]"]
  Εξάρτημα1 = 4053 [package="DIP (Dual Inline) [THT]"]  # not connected
  U1_1 = 4053 [package="DIP (Dual Inline) [THT]"]  # not connected
  U1_2 = 4053 [package="DIP (Dual Inline) [THT]"]  # not connected
  U1_3 = 4053 [package="DIP (Dual Inline) [THT]"]  # not connected
  IC1 = MCP23017 I2C I/O Expander [part_number=MCP23S17(IC0)]
  U2 = 4053 [part_number=74HC4053(IC1) package="DIP (Dual Inline) [THT]"]
  U2_3 = 4053 [package="DIP (Dual Inline) [THT]"]  # not connected
  U2_2 = 4053 [package="DIP (Dual Inline) [THT]"]  # not connected
  U2_1 = 4053 [package="DIP (Dual Inline) [THT]"]  # not connected
  Εξάρτημα2 = 4053 [package="DIP (Dual Inline) [THT]"]  # not connected
  R1 = Resistor [tolerance=±5% resistance=3.3k part_number="Pull down" package="0402 [SMD]"]
  J8 = male pin header, 1 pin [form="♂ (male)"]
  R2 = Resistor [tolerance=±5% resistance=3.3k part_number="Pull down" package="0402 [SMD]"]
  R3 = Resistor [tolerance=±5% resistance=3.3k part_number="Pull down" package="0402 [SMD]"]  # not connected
  R4 = Resistor [tolerance=±5% resistance=3.3k part_number="Pull down" package="0402 [SMD]"]
  J9 = male pin header, 1 pin [form="♂ (male)"]
  J11 = male pin header, 1 pin [form="♂ (male)"]
  J12 = male pin header, 1 pin [form="♂ (male)"]
  J13 = male pin header, 1 pin [form="♂ (male)"]
  J14 = male pin header, 1 pin [form="♂ (male)"]
  J17 = male pin header, 1 pin [form="♂ (male)"]
  J18 = male pin header, 1 pin [form="♂ (male)"]
  J19 = male pin header, 1 pin [form="♂ (male)"]
  J21 = male pin header, 1 pin [form="♂ (male)"]
  J23 = male pin header, 1 pin [form="♂ (male)"]
  J25 = male pin header, 1 pin [form="♂ (male)"]
  J26 = male pin header, 1 pin [form="♂ (male)"]
  R5 = Resistor [tolerance=±5% resistance=3.3k part_number="Pull down" package="0402 [SMD]"]
  R6 = Resistor [tolerance=±5% resistance=3.3k part_number="Pull down" package="0402 [SMD]"]
  R7 = Resistor [tolerance=±5% resistance=3.3k part_number="Pull down" package="0402 [SMD]"]
  R8 = Resistor [tolerance=±5% resistance=3.3k part_number="Pull down" package="0402 [SMD]"]  # not connected
  J27 = male pin header, 1 pin [form="♂ (male)"]
  J28 = male pin header, 1 pin [form="♂ (male)"]
  J29 = male pin header, 1 pin [form="♂ (male)"]
  J30 = male pin header, 1 pin [form="♂ (male)"]
  J31 = male pin header, 1 pin [form="♂ (male)"]
  J32 = male pin header, 1 pin [form="♂ (male)"]
  J33 = male pin header, 1 pin [form="♂ (male)"]
  J34 = male pin header, 1 pin [form="♂ (male)"]
  J35 = male pin header, 1 pin [form="♂ (male)"]
  J36 = male pin header, 1 pin [form="♂ (male)"]
  J37 = male pin header, 1 pin [form="♂ (male)"]
  J38 = male pin header, 1 pin [form="♂ (male)"]
  J41 = male pin header, 1 pin [form="♂ (male)"]
  J42 = male pin header, 1 pin [form="♂ (male)"]
  J43 = male pin header, 1 pin [form="♂ (male)"]
  J44 = male pin header, 1 pin [form="♂ (male)"]
  J45 = male pin header, 1 pin [form="♂ (male)"]
  J46 = male pin header, 1 pin [form="♂ (male)"]
  J47 = male pin header, 1 pin [form="♂ (male)"]
  J48 = male pin header, 1 pin [form="♂ (male)"]
  J49 = male pin header, 1 pin [form="♂ (male)"]
  J50 = male pin header, 1 pin [form="♂ (male)"]
  J51 = male pin header, 1 pin [form="♂ (male)"]
  J52 = male pin header, 1 pin [form="♂ (male)"]
  J53 = male pin header, 1 pin [form="♂ (male)"]
  J54 = male pin header, 1 pin [form="♂ (male)"]
  J55 = male pin header, 1 pin [form="♂ (male)"]
  J56 = male pin header, 1 pin [form="♂ (male)"]
  J57 = male pin header, 1 pin [form="♂ (male)"]
  J58 = male pin header, 1 pin [form="♂ (male)"]
  J59 = male pin header, 1 pin [form="♂ (male)"]
  J60 = male pin header, 1 pin [form="♂ (male)"]
  J61 = male pin header, 1 pin [form="♂ (male)"]
  J62 = male pin header, 1 pin [form="♂ (male)"]
  J63 = male pin header, 1 pin [form="♂ (male)"]
  J64 = male pin header, 1 pin [form="♂ (male)"]
  J65 = male pin header, 1 pin [form="♂ (male)"]
  J66 = male pin header, 1 pin [form="♂ (male)"]
  J67 = male pin header, 1 pin [form="♂ (male)"]
  J68 = male pin header, 1 pin [form="♂ (male)"]
  J69 = male pin header, 1 pin [form="♂ (male)"]
  J70 = male pin header, 1 pin [form="♂ (male)"]
  J71 = male pin header, 1 pin [form="♂ (male)"]
  J72 = male pin header, 1 pin [form="♂ (male)"]
  J73 = male pin header, 1 pin [form="♂ (male)"]
  J74 = male pin header, 1 pin [form="♂ (male)"]
  J75 = male pin header, 1 pin [form="♂ (male)"]
  J76 = male pin header, 1 pin [form="♂ (male)"]
  J77 = male pin header, 1 pin [form="♂ (male)"]
  J80 = male pin header, 1 pin [form="♂ (male)"]
  J106 = male pin header, 1 pin [form="♂ (male)"]
  J107 = male pin header, 1 pin [form="♂ (male)"]
  J108 = male pin header, 1 pin [form="♂ (male)"]
  J109 = male pin header, 1 pin [form="♂ (male)"]
  R9 = Resistor [tolerance=±5% resistance=3.3k package="0402 [SMD]"]
  Εξάρτημα3 = Adafruit T-Cobbler Plus [part_number="Adafruit #1989 and #2028"]
  R10 = Resistor [tolerance=±5% resistance=3.3k package="0402 [SMD]"]
  R11 = Resistor [tolerance=±5% resistance=3.3k package="0402 [SMD]"]
  R12 = Resistor [tolerance=±5% resistance=3.3k package="0402 [SMD]"]
  J110 = male pin header, 1 pin [form="♂ (male)"]
  J111 = male pin header, 1 pin [form="♂ (male)"]
  J112 = male pin header, 1 pin [form="♂ (male)"]
  J113 = male pin header, 1 pin [form="♂ (male)"]
  J114 = male pin header, 1 pin [form="♂ (male)"]
  J115 = male pin header, 1 pin [form="♂ (male)"]
  J116 = male pin header, 1 pin [form="♂ (male)"]
  J117 = male pin header, 1 pin [form="♂ (male)"]
  JP37 = Header 6 [package=molex-1x6-ra]
  JP39 = Header 6 [package=molex-1x6-ra]
  JP40 = Header 6 [package=molex-1x6-ra]
  J118 = male pin header, 1 pin [form="♂ (male)"]
  J119 = male pin header, 1 pin [form="♂ (male)"]
  J120 = male pin header, 1 pin [form="♂ (male)"]
  J121 = male pin header, 1 pin [form="♂ (male)"]
  J122 = male pin header, 1 pin [form="♂ (male)"]
  J123 = male pin header, 1 pin [form="♂ (male)"]
  J124 = male pin header, 1 pin [form="♂ (male)"]
  J126 = male pin header, 1 pin [form="♂ (male)"]
  J128 = male pin header, 1 pin [form="♂ (male)"]
  J129 = male pin header, 1 pin [form="♂ (male)"]
  J130 = male pin header, 1 pin [form="♂ (male)"]
  J135 = male pin header, 1 pin [form="♂ (male)"]
  J136 = male pin header, 1 pin [form="♂ (male)"]
  J137 = male pin header, 1 pin [form="♂ (male)"]
  J138 = male pin header, 1 pin [form="♂ (male)"]
  J139 = male pin header, 1 pin [form="♂ (male)"]
  J140 = male pin header, 1 pin [form="♂ (male)"]
  J141 = male pin header, 1 pin [form="♂ (male)"]
  J142 = male pin header, 1 pin [form="♂ (male)"]
  JP41 = Header 6 [package=molex-1x6-ra]
  J143 = male pin header, 1 pin [form="♂ (male)"]
  J144 = male pin header, 1 pin [form="♂ (male)"]
  J145 = male pin header, 1 pin [form="♂ (male)"]
  J146 = male pin header, 1 pin [form="♂ (male)"]
  J147 = male pin header, 1 pin [form="♂ (male)"]
  J148 = male pin header, 1 pin [form="♂ (male)"]
  R13 = Resistor [tolerance=±5% resistance=3.3k package="0402 [SMD]"]
  R14 = Resistor [tolerance=±5% resistance=3.3k package="0402 [SMD]"]
  R15 = Resistor [tolerance=±5% resistance=3.3k package="0402 [SMD]"]
  R16 = Resistor [tolerance=±5% resistance=3.3k package="0402 [SMD]"]
  J149 = male pin header, 1 pin [form="♂ (male)"]
  J150 = male pin header, 1 pin [form="♂ (male)"]
  J151 = male pin header, 1 pin [form="♂ (male)"]
  J152 = male pin header, 1 pin [form="♂ (male)"]
  J153 = male pin header, 1 pin [form="♂ (male)"]
  J154 = male pin header, 1 pin [form="♂ (male)"]
  J155 = male pin header, 1 pin [form="♂ (male)"]
  J156 = male pin header, 1 pin [form="♂ (male)"]
  J157 = male pin header, 1 pin [form="♂ (male)"]
  J158 = male pin header, 1 pin [form="♂ (male)"]
  J159 = male pin header, 1 pin [form="♂ (male)"]

nets:
  N1: M1.pin1, U1.connector11, R1.Pin_1, J9.pin1, J29.pin1, J31.pin1
  N2: M1.pin2, U1.connector12, J11.pin1, J17.pin1, J18.pin1
  N3: M1.pin3, M1.pin4, IC1.GPA3, J56.pin1, J57.pin1
  N4: M1.pin7, M2.pin7, U1.connector15, J27.pin1, J139.pin1, J140.pin1, JP41.1
  N5: M1.pin8, M2.pin8, U1.connector5, U1.connector6, U1.connector7, R1.Pin_0, R2.Pin_0, R4.Pin_0, J14.pin1, J41.pin1, JP40.1, J146.pin1, J147.pin1, J148.pin1
  N6: M1.pin11, JP37.2
  N7: M1.pin12, JP39.2
  N8: M2.pin1, U1.connector1, R2.Pin_1, R4.Pin_1, J13.pin1, J37.pin1, J38.pin1
  N9: M2.pin2, U1.connector0, J12.pin1, J35.pin1, J36.pin1
  N10: M2.pin3, M2.pin4, IC1.GPA4, J54.pin1, J55.pin1
  N11: M2.pin11, JP37.1
  N12: M2.pin12, JP39.1
  N13: M3.pin1, U2.connector1, J25.pin1, J75.pin1, J77.pin1
  N14: M3.pin2, U2.connector0, J19.pin1, R7.Pin_0, J74.pin1, J76.pin1
  N15: M3.pin3, M3.pin4, IC1.GPB4, J47.pin1, J48.pin1
  N16: M3.pin7, M4.pin7, U2.connector15, J64.pin1, J141.pin1, J142.pin1, JP41.3
  N17: M3.pin8, M4.pin8, IC1.A0, IC1.A1, IC1.A2, IC1.VSS, U2.connector5, U2.connector6, U2.connector7, J21.pin1, R5.Pin_1, R6.Pin_1, R7.Pin_1, J45.pin1, J61.pin1, J62.pin1, J63.pin1, J80.pin1, JP40.6, J118.pin1, J119.pin1, J120.pin1, J121.pin1, J122.pin1, J123.pin1, J124.pin1, J126.pin1, J128.pin1, J129.pin1, J130.pin1, J143.pin1, J144.pin1, J145.pin1, J157.pin1, J158.pin1, J159.pin1
  N18: M3.pin11, JP37.4
  N19: M3.pin12, JP39.3
  N20: M4.pin1, U2.connector11, J26.pin1, R6.Pin_0, J70.pin1, J71.pin1
  N21: M4.pin2, U2.connector12, J23.pin1, R5.Pin_0, J68.pin1, J69.pin1
  N22: M4.pin3, M4.pin4, IC1.GPB3, J49.pin1, J50.pin1
  N23: M4.pin11, JP37.3
  N24: M4.pin12, JP39.4
  N25: U1.connector8, IC1.GPA2, J34.pin1, J58.pin1
  N26: U1.connector9, IC1.GPA1, J33.pin1, J59.pin1
  N27: U1.connector10, IC1.GPA0, J32.pin1, J60.pin1
  N28: U1.connector13, J30.pin1, R14.Pin_0, J154.pin1
  N29: U1.connector14, J28.pin1, R13.Pin_0, J149.pin1
  N30: IC1.GPB0, U2.connector10, J53.pin1, J66.pin1
  N31: IC1.GPB1, U2.connector9, J52.pin1, J72.pin1
  N32: IC1.GPB2, U2.connector8, J51.pin1, J73.pin1
  N33: IC1.VDD, J46.pin1, JP41.2
  N34: IC1.CS, J44.pin1, R9.Pin_0, J113.pin1
  N35: IC1.SCK, J43.pin1, J106.pin1, R12.Pin_0
  N36: IC1.SI, J42.pin1, J107.pin1, R11.Pin_0
  N37: IC1.SO, J8.pin1, J108.pin1, R10.Pin_0
  N38: U2.connector13, J67.pin1, R16.Pin_0, J156.pin1
  N39: U2.connector14, J65.pin1, R15.Pin_0, J155.pin1
  N40: J109.pin1, R9.Pin_1, Εξάρτημα3.CE0, J114.pin1
  N41: Εξάρτημα3.MOSI, R11.Pin_1, J110.pin1, J117.pin1
  N42: Εξάρτημα3.MISO, R10.Pin_1, J111.pin1, J115.pin1
  N43: Εξάρτημα3.SCLK, R12.Pin_1, J112.pin1, J116.pin1
  N44: Εξάρτημα3.GPIO13, J136.pin1, R14.Pin_1, J151.pin1
  N45: Εξάρτημα3.GPIO19, J135.pin1, R13.Pin_1, J150.pin1
  N46: Εξάρτημα3.GPIO18, J138.pin1, R16.Pin_1, J153.pin1
  N47: Εξάρτημα3.GPIO12, J137.pin1, R15.Pin_1, J152.pin1

notes:
  +24V Power Source
  +5V Buck Converter
  OVERAL TODO
  The mirroring left-right motors motion will be handle in source code at functions like moveForwardFrontLeftMotor(), moveBackwardFrontLeftMotor(), etc for the other 3 motors.
  GND
  -24V Power Source
  Connect to the closest PCB Ground

custom parts:
  BTS7960: BTS7960 43A Peak Power H-Bridge PWM Motor Driver
  4053: A 4053 three element single throw double pole analog switch in schematic subpart format.
  4053: A 4053 three element single throw double pole analog switch in schematic subpart format.
  4053: A 4053 three element single throw double pole analog switch in schematic subpart format.
  4053: A 4053 three element single throw double pole analog switch in schematic subpart format.
  4053: A 4053 three element single throw double pole analog switch in schematic subpart format.
  MCP23017 I2C I/O Expander: The MCP23017 uses two i2c pins (these can be shared with other i2c devices), and in exchange gives you 16 general purpose pins. You can set each of 16 pins to be input, output, input with a pullup or open drain. There's even the ability to get an interrupt via an external pin when any of the inputs change so you don't have to keep polling the chip.
  Adafruit T-Cobbler Plus: The Raspberry Pi has landed on the Maker World like a 40-GPIO pinned, quad-USB ported, credit card sized bomb of DIY joy. And while you can use most of our great Model B accessories by hooking up our downgrade cable, its probably a good time to upgrade your set up and accessorize using all of the 40 pins. That's why we now carry the Assembled Adafruit Pi T-Cobbler Plus - Breakout + Cable for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
