# Fritzing sketch Buck Converters (saved by Fritzing 0.9.3b)
perfboards: 1

parts:
  M1 = RioRand LM2596 [part_number="Servo Steering (6V)"]
  M2 = RioRand LM2596 [part_number="Logic Use (5V)"]
  M3 = RioRand LM2596 [part_number="Logic Use (3V3)"]
  M4 = RioRand LM2596 [part_number="Power Use (10V-12V)"]
  VCC1 = Battery block 9V

nets:
  N1: M1.Pin_1, M2.Pin_1, M3.Pin_1, M4.Pin_1, VCC1.+
  N2: M1.Pin_2, M2.Pin_2, M3.Pin_2, M4.Pin_2, VCC1.-
  N3: M2.Pin_4, M3.Pin_4, M4.Pin_4

notes:
  ... to Servo Backup Circuit
  ≃ 24V
  ... to RasPi GND
  Solder as you go!
