# Fritzing sketch Regulator 5V (saved by Fritzing 0.9.3b)
stripboards: 1
perfboards: 1

parts:
  U1 = Voltage Regulator [package=to220-adj]
  R1 = Resistor [tolerance=±5% resistance=270 part_number=R1 package="2010 [SMD]"]
  R2 = Resistor [tolerance=±5% resistance=820 part_number=810Ω package="2010 [SMD]"]
  C2 = Capacitor Polarized [part_number=100nF package=panasonic_c]
  C1 = Capacitor Polarized [part_number=100nF package=panasonic_c]

nets:
  N1: U1.ADJ, R1.Pin_0, R2.Pin_0
  N2: U1.IN, C1.+
  N3: U1.OUT, R1.Pin_1, C2.+
  N4: R2.Pin_1, C2.-, C1.-

notes:
  Σημαντικά Links:
  1. https://www.allaboutcircuits.com/tools/parallel-resistance-calculator/
  2. https://www.banggood.com/560-Pcs-1-ohm-to-10M-ohm-14W-5-Metal-Film-Resistor-56-Value-Assorted-Kit-p-1072159.html?akmClientCountry=GR&rmmds=detail-left-hotproducts__2&cur_warehouse=CN
  3. http://www.learningaboutelectronics.com/Articles/LM317-voltage-regulator
  4. https://www.electronics-tutorials.ws/blog/variable-voltage-power-supply.html
  5. https://circuitdigest.com/calculators/lm317-resistor-voltage-calculator
