# Fritzing sketch Servo Controller (saved by Fritzing 0.9.3b)
perfboards: 1
breadboards: 2

parts:
  J1 = Basic Servo [part_number=MG996R]
  R1 = Resistor [tolerance=±5% resistance=5.5k package="0402 [SMD]"]
  Εξάρτημα1 = Adafruit T-Cobbler Plus [part_number="Adafruit #1989 and #2028"]
  J85 = male pin header, 1 pin [form="♂ (male)"]
  J86 = male pin header, 1 pin [form="♂ (male)"]
  D3 = P1000K [part_number="Rpi Diode (1N5822)"]
  D4 = P1000K [part_number="Buck Converter Diode (1N5822)"]
  J87 = male pin header, 1 pin [form="♂ (male)"]
  J88 = male pin header, 1 pin [form="♂ (male)"]
  J89 = male pin header, 1 pin [form="♂ (male)"]
  J90 = male pin header, 1 pin [form="♂ (male)"]
  J91 = male pin header, 1 pin [form="♂ (male)"]
  J92 = male pin header, 1 pin [form="♂ (male)"]
  JP17 = Header 6 [package=molex-1x6-ra]
  JP35 = Header 6 [package=molex-1x6-ra]
  JP36 = Header 6 [package=molex-1x6-ra]
  R15 = Resistor [tolerance=±5% resistance=3.3k package="0402 [SMD]"]
  R16 = Resistor [tolerance=±5% resistance=3.3k package="0402 [SMD]"]

nets:
  N1: J1.gnd, J87.pin1, J88.pin1, J90.pin1, JP35.6, JP36.6
  N2: J1.vcc, D3.cathode, J89.pin1
  N3: J1.pulse, R1.Pin_1, J85.pin1
  N4: R1.Pin_0, Εξάρτημα1.GPIO23, J86.pin1
  N5: Εξάρτημα1.+3.3V, R15.Pin_1
  N6: Εξάρτημα1.+5V, R16.Pin_0
  N7: D3.anode, J91.pin1, JP36.1
  N8: D4.anode, J92.pin1, JP17.1

notes:
  The less current possible, just to function properly.
  MG996R servo has a running current of 500mA to 900mA @6V and a stall current of 2.5A @ 6V
  +Servo Buck Converter
  Inspired by the book "The Art of Electronics" pg 36 Fig 1.71
  GND
  Step up Voltage Regulator

custom parts:
  Adafruit T-Cobbler Plus: The Raspberry Pi has landed on the Maker World like a 40-GPIO pinned, quad-USB ported, credit card sized bomb of DIY joy. And while you can use most of our great Model B accessories by hooking up our downgrade cable, its probably a good time to upgrade your set up and accessorize using all of the 40 pins. That's why we now carry the Assembled Adafruit Pi T-Cobbler Plus - Breakout + Cable for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
