# Fritzing sketch BTS7960 Connection System (saved by Fritzing 0.9.3b)
breadboards: 5

parts:
  M1 = BTS7960 [part_number=BTS7960(IC0)]
  M2 = BTS7960 [part_number=BTS7960(IC1)]
  M3 = BTS7960 [part_number=BTS7960(IC3)]
  M4 = BTS7960 [part_number=BTS7960(IC2)]
  U1 = 4053 [part_number=74HC4053(IC0) package="DIP (Dual Inline) [THT]"]
  Εξάρτημα1 = 4053 [package="DIP (Dual Inline) [THT]"]  # not connected
  U1_1 = 4053 [package="DIP (Dual Inline) [THT]"]  # not connected
  U1_2 = 4053 [package="DIP (Dual Inline) [THT]"]  # not connected
  U1_3 = 4053 [package="DIP (Dual Inline) [THT]"]  # not connected
  IC1 = MCP23017 I2C I/O Expander [part_number=MCP23S17(IC0)]
  U2 = 4053 [part_number=74HC4053(IC1) package="DIP (Dual Inline) [THT]"]
  U2_3 = 4053 [package="DIP (Dual Inline) [THT]"]  # not connected
  U2_2 = 4053 [package="DIP (Dual Inline) [THT]"]  # not connected
  U2_1 = 4053 [package="DIP (Dual Inline) [THT]"]  # not connected
  Εξάρτημα2 = 4053 [package="DIP (Dual Inline) [THT]"]  # not connected
  R9 = Resistor [tolerance=±5% resistance=3.3k package="0402 [SMD]"]
  R10 = Resistor [tolerance=±5% resistance=3.3k package="0402 [SMD]"]
  R11 = Resistor [tolerance=±5% resistance=3.3k package="0402 [SMD]"]
  R12 = Resistor [tolerance=±5% resistance=3.3k package="0402 [SMD]"]
  JP37 = Header 6 [package=molex-1x6-ra]
  JP39 = Header 6 [package=molex-1x6-ra]
  JP40 = Header 6 [package=molex-1x6-ra]
  JP41 = Header 6 [package=molex-1x6-ra]
  R13 = Resistor [tolerance=±5% resistance=3.3k package="0402 [SMD]"]
  R14 = Resistor [tolerance=±5% resistance=3.3k package="0402 [SMD]"]
  R15 = Resistor [tolerance=±5% resistance=3.3k package="0402 [SMD]"]
  R16 = Resistor [tolerance=±5% resistance=3.3k package="0402 [SMD]"]
  Εξάρτημα3 = Adafruit T-Cobbler Plus [part_number="Adafruit #1989 and #2028"]
  R17 = Resistor [tolerance=±5% resistance=3.3k part_number="Pull down" package="0402 [SMD]"]
  R18 = Resistor [tolerance=±5% resistance=3.3k part_number="Pull down" package="0402 [SMD]"]
  R19 = Resistor [tolerance=±5% resistance=3.3k part_number="Pull down" package="0402 [SMD]"]
  R20 = Resistor [tolerance=±5% resistance=3.3k part_number="Pull down" package="0402 [SMD]"]
  R21 = Resistor [tolerance=±5% resistance=3.3k part_number="Pull down" package="0402 [SMD]"]
  R22 = Resistor [tolerance=±5% resistance=3.3k part_number="Pull down" package="0402 [SMD]"]
  R23 = Resistor [tolerance=±5% resistance=3.3k part_number="Pull down" package="0402 [SMD]"]
  R24 = Resistor [tolerance=±5% resistance=3.3k part_number="Pull down" package="0402 [SMD]"]
  R25 = Resistor [tolerance=±5% resistance=3.3k package="0402 [SMD]"]
  R26 = Resistor [tolerance=±5% resistance=3.3k package="0402 [SMD]"]

nets:
  N1: M1.pin1, U1.connector11, R18.Pin_0
  N2: M1.pin2, U1.connector12, R17.Pin_0
  N3: M1.pin3, M1.pin4, IC1.GPA3
  N4: M1.pin7, M2.pin7, U1.connector15, JP41.1
  N5: M1.pin8, M2.pin8, U1.connector5, U1.connector6, U1.connector7, JP40.1, R17.Pin_1, R18.Pin_1, R19.Pin_1, R20.Pin_1
  N6: M1.pin11, JP37.2
  N7: M1.pin12, JP39.2
  N8: M2.pin1, U1.connector1, R19.Pin_0
  N9: M2.pin2, U1.connector0, R20.Pin_0
  N10: M2.pin3, M2.pin4, IC1.GPA4
  N11: M2.pin11, JP37.1
  N12: M2.pin12, JP39.1
  N13: M3.pin1, U2.connector1, R21.Pin_0
  N14: M3.pin2, U2.connector0, R22.Pin_0
  N15: M3.pin3, M3.pin4, IC1.GPB4
  N16: M3.pin7, M4.pin7, IC1.VDD, U2.connector15, JP41.2
  N17: M3.pin8, M4.pin8, IC1.A0, IC1.A1, IC1.A2, IC1.VSS, U2.connector5, U2.connector6, U2.connector7, R21.Pin_1, R22.Pin_1, R23.Pin_1, R24.Pin_1
  N18: M3.pin11, JP37.4
  N19: M3.pin12, JP39.3
  N20: M4.pin1, U2.connector11, R23.Pin_0
  N21: M4.pin2, U2.connector12, R24.Pin_0
  N22: M4.pin3, M4.pin4, IC1.GPB3
  N23: M4.pin11, JP37.3
  N24: M4.pin12, JP39.4
  N25: U1.connector8, IC1.GPA2
  N26: U1.connector9, IC1.GPA1
  N27: U1.connector10, IC1.GPA0
  N28: U1.connector13, R14.Pin_1
  N29: U1.connector14, R13.Pin_1
  N30: IC1.GPB0, U2.connector10
  N31: IC1.GPB1, U2.connector9
  N32: IC1.GPB2, U2.connector8
  N33: IC1.CS, R9.Pin_0
  N34: IC1.SCK, R12.Pin_1
  N35: IC1.SI, R11.Pin_1
  N36: IC1.SO, R10.Pin_1
  N37: U2.connector13, R16.Pin_0
  N38: U2.connector14, R15.Pin_0
  N39: R9.Pin_1, Εξάρτημα3.CE0
  N40: JP40.6, Εξάρτημα3.GND
  N41: R15.Pin_1, Εξάρτημα3.GPIO12
  N42: R16.Pin_1, Εξάρτημα3.GPIO18
  N43: Εξάρτημα3.+3.3V, R25.Pin_0
  N44: Εξάρτημα3.+5V, R26.Pin_1

notes:
  +24V Power Source
  +5V Buck Converter
  OVERAL TODO
  The mirroring left-right motors motion will be handle in source code at functions like moveForwardFrontLeftMotor(), moveBackwardFrontLeftMotor(), etc for the other 3 motors.
  GNDs
  -24V Power Source
  Connect to the closest PCB Ground
  The less current possible, just to function properly.

custom parts:
  BTS7960: BTS7960 43A Peak Power H-Bridge PWM Motor Driver
  4053: A 4053 three element single throw double pole analog switch in schematic subpart format.
  4053: A 4053 three element single throw double pole analog switch in schematic subpart format.
  4053: A 4053 three element single throw double pole analog switch in schematic subpart format.
  4053: A 4053 three element single throw double pole analog switch in schematic subpart format.
  4053: A 4053 three element single throw double pole analog switch in schematic subpart format.
  MCP23017 I2C I/O Expander: The MCP23017 uses two i2c pins (these can be shared with other i2c devices), and in exchange gives you 16 general purpose pins. You can set each of 16 pins to be input, output, input with a pullup or open drain. There's even the ability to get an interrupt via an external pin when any of the inputs change so you don't have to keep polling the chip.
  Adafruit T-Cobbler Plus: The Raspberry Pi has landed on the Maker World like a 40-GPIO pinned, quad-USB ported, credit card sized bomb of DIY joy. And while you can use most of our great Model B accessories by hooking up our downgrade cable, its probably a good time to upgrade your set up and accessorize using all of the 40 pins. That's why we now carry the Assembled Adafruit Pi T-Cobbler Plus - Breakout + Cable for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
