# Fritzing sketch Water Cooling Conection System (saved by Fritzing 0.9.3b)
stripboards: 1
breadboards: 3

parts:
  M1 = DC Motor [part_number="Water Pump"]
  IC2 = MCP23017 I2C I/O Expander [part_number=MCP23S17(IC1)]
  IC3 = L293D [part_number=L293D(IC0) package=THT]
  J65 = male pin header, 1 pin [form="♂ (male)"]
  J66 = male pin header, 1 pin [form="♂ (male)"]
  J67 = male pin header, 1 pin [form="♂ (male)"]
  J68 = male pin header, 1 pin [form="♂ (male)"]
  J69 = male pin header, 1 pin [form="♂ (male)"]
  J70 = male pin header, 1 pin [form="♂ (male)"]
  J72 = male pin header, 1 pin [form="♂ (male)"]
  J73 = male pin header, 1 pin [form="♂ (male)"]
  J74 = male pin header, 1 pin [form="♂ (male)"]
  F1 = Fan - Ventilador [package=THT]
  JP16 = Header 6 [package=molex-1x6-ra]
  JP33 = Header 6 [package=molex-1x6-ra]
  J107 = male pin header, 1 pin [form="♂ (male)"]
  Εξάρτημα4 = Adafruit T-Cobbler Plus [part_number="Adafruit #1989 and #2028"]
  R30 = Resistor [tolerance=±5% resistance=3.3k package="0402 [SMD]"]
  R31 = Resistor [tolerance=±5% resistance=3.3k package="0402 [SMD]"]  # not connected
  R33 = Resistor [tolerance=±5% resistance=3.3k package="0402 [SMD]"]
  JP41 = Header 6 [package=molex-1x6-ra]
  R34 = Resistor [tolerance=±5% resistance=3.3k package="0402 [SMD]"]
  R35 = Resistor [tolerance=±5% resistance=3.3k package="0402 [SMD]"]
  R36 = Resistor [tolerance=±5% resistance=3.3k package="0402 [SMD]"]
  IC4 = MCP23017 I2C I/O Expander [part_number=MCP23S17(IC0)]

nets:
  N1: M1.pin_1, IC3.0V, J68.pin1, J69.pin1, J70.pin1, F1.GND, JP41.1
  N2: M1.pin_2, IC3.Out_1_(_Controlled_by_Enable_1_), J67.pin1
  VDD: IC2.A0, IC2.VDD, IC3.Enable_1, IC3.+V, J65.pin1, JP33.3, J107.pin1, IC4.VDD
  VSS: IC2.A1, IC2.A2, IC2.VSS, IC4.A0, IC4.A1, IC4.A2, IC4.VSS
  N3: IC2.GPA0, IC3.In_1, J66.pin1
  N4: IC2.GPA1, IC3.In_2, J73.pin1
  N5: IC2.CS, R33.Pin_0, IC4.CS
  N6: IC2.SCK, R36.Pin_1, IC4.SCK
  N7: IC2.SI, R35.Pin_1, IC4.SI
  N8: IC2.SO, R34.Pin_1, IC4.SO
  N9: IC3.Out_2_(_Controlled_by_Enable_1_), J72.pin1, F1.5V
  N10: IC3.+Vmotor, J74.pin1, JP16.1
  N11: Εξάρτημα4.+5V, R30.Pin_1
  N12: Εξάρτημα4.GND, JP41.6
  N13: Εξάρτημα4.CE0, R33.Pin_1

notes:
  +5V Buck Converter
  +(10V-12V) Buck Converter
  Max 12V
  Max 12V and 0.3A
  The less current possible, just to function properly.
  GNDs

custom parts:
  MCP23017 I2C I/O Expander: The MCP23017 uses two i2c pins (these can be shared with other i2c devices), and in exchange gives you 16 general purpose pins. You can set each of 16 pins to be input, output, input with a pullup or open drain. There's even the ability to get an interrupt via an external pin when any of the inputs change so you don't have to keep polling the chip.
  Fan - Ventilador: Ventilador de 2 pines, se encuentra comunmente en computadoras de escritorio
  Adafruit T-Cobbler Plus: The Raspberry Pi has landed on the Maker World like a 40-GPIO pinned, quad-USB ported, credit card sized bomb of DIY joy. And while you can use most of our great Model B accessories by hooking up our downgrade cable, its probably a good time to upgrade your set up and accessorize using all of the 40 pins. That's why we now carry the Assembled Adafruit Pi T-Cobbler Plus - Breakout + Cable for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
