# Fritzing sketch Water Cooling Conection System (saved by Fritzing 0.9.3b)
stripboards: 3
perfboards: 1

parts:
  M1 = DC Motor [part_number="Water Pump"]
  IC2 = MCP23017 I2C I/O Expander [part_number=MCP23S17(IC1)]
  IC3 = L293D [part_number=L293D(IC0) package=THT]
  J65 = male pin header, 1 pin [form="♂ (male)"]
  J66 = male pin header, 1 pin [form="♂ (male)"]
  J67 = male pin header, 1 pin [form="♂ (male)"]
  J68 = male pin header, 1 pin [form="♂ (male)"]
  J69 = male pin header, 1 pin [form="♂ (male)"]
  J70 = male pin header, 1 pin [form="♂ (male)"]
  J72 = male pin header, 1 pin [form="♂ (male)"]
  J73 = male pin header, 1 pin [form="♂ (male)"]
  J74 = male pin header, 1 pin [form="♂ (male)"]
  J75 = male pin header, 1 pin [form="♂ (male)"]
  J76 = male pin header, 1 pin [form="♂ (male)"]
  J77 = male pin header, 1 pin [form="♂ (male)"]
  J78 = male pin header, 1 pin [form="♂ (male)"]
  J79 = male pin header, 1 pin [form="♂ (male)"]
  J80 = male pin header, 1 pin [form="♂ (male)"]
  J81 = male pin header, 1 pin [form="♂ (male)"]
  J82 = male pin header, 1 pin [form="♂ (male)"]
  J83 = male pin header, 1 pin [form="♂ (male)"]
  J84 = male pin header, 1 pin [form="♂ (male)"]
  J85 = male pin header, 1 pin [form="♂ (male)"]
  F1 = Fan - Ventilador [package=THT]
  R2 = Resistor [tolerance=±5% resistance=3.3k package="0402 [SMD]"]
  R3 = Resistor [tolerance=±5% resistance=3.3k package="0402 [SMD]"]
  R4 = Resistor [tolerance=±5% resistance=3.3k package="0402 [SMD]"]
  R5 = Resistor [tolerance=±5% resistance=3.3k package="0402 [SMD]"]
  J88 = male pin header, 1 pin [form="♂ (male)"]
  Εξάρτημα2 = Adafruit T-Cobbler Plus [part_number="Adafruit #1989 and #2028"]
  J89 = male pin header, 1 pin [form="♂ (male)"]
  J90 = male pin header, 1 pin [form="♂ (male)"]
  J91 = male pin header, 1 pin [form="♂ (male)"]
  J92 = male pin header, 1 pin [form="♂ (male)"]
  J93 = male pin header, 1 pin [form="♂ (male)"]
  J94 = male pin header, 1 pin [form="♂ (male)"]
  J95 = male pin header, 1 pin [form="♂ (male)"]
  J96 = male pin header, 1 pin [form="♂ (male)"]
  J99 = male pin header, 1 pin [form="♂ (male)"]
  J100 = male pin header, 1 pin [form="♂ (male)"]
  J101 = male pin header, 1 pin [form="♂ (male)"]
  J102 = male pin header, 1 pin [form="♂ (male)"]
  J103 = male pin header, 1 pin [form="♂ (male)"]
  J104 = male pin header, 1 pin [form="♂ (male)"]
  J105 = male pin header, 1 pin [form="♂ (male)"]
  J106 = male pin header, 1 pin [form="♂ (male)"]
  JP16 = Header 6 [package=molex-1x6-ra]
  JP33 = Header 6 [package=molex-1x6-ra]
  JP34 = Header 6 [package=molex-1x6-ra]
  J107 = male pin header, 1 pin [form="♂ (male)"]
  J108 = male pin header, 1 pin [form="♂ (male)"]
  J109 = male pin header, 1 pin [form="♂ (male)"]
  J110 = male pin header, 1 pin [form="♂ (male)"]
  J111 = male pin header, 1 pin [form="♂ (male)"]
  J112 = male pin header, 1 pin [form="♂ (male)"]
  J113 = male pin header, 1 pin [form="♂ (male)"]
  J114 = male pin header, 1 pin [form="♂ (male)"]

nets:
  VSS: M1.pin_1, IC2.A1, IC2.A2, IC2.VSS, IC3.0V, J68.pin1, J69.pin1, J70.pin1, J76.pin1, J83.pin1, J84.pin1, F1.GND, J99.pin1, J103.pin1, J104.pin1, J105.pin1, J106.pin1, JP34.6, J109.pin1, J110.pin1, J111.pin1, J112.pin1, J113.pin1, J114.pin1
  N1: M1.pin_2, IC3.Out_1_(_Controlled_by_Enable_1_), J67.pin1
  N2: IC2.A0, J85.pin1, JP33.2
  N3: IC2.GPA0, IC3.In_1, J66.pin1, J82.pin1
  N4: IC2.GPA1, IC3.In_2, J73.pin1, J81.pin1
  N5: IC2.VDD, IC3.Enable_1, IC3.+V, J65.pin1, J75.pin1, JP33.1, J107.pin1, J108.pin1
  N6: IC2.CS, J77.pin1, R5.Pin_0, J93.pin1
  N7: IC2.SCK, J78.pin1, R2.Pin_0, J90.pin1
  N8: IC2.SI, J79.pin1, R4.Pin_0, J91.pin1
  N9: IC2.SO, J80.pin1, R3.Pin_0, J92.pin1
  N10: IC3.Out_2_(_Controlled_by_Enable_1_), J72.pin1, F1.5V
  N11: IC3.+Vmotor, J74.pin1, JP16.1
  N12: R2.Pin_1, Εξάρτημα2.SCLK, J89.pin1, J100.pin1
  N13: R3.Pin_1, Εξάρτημα2.MISO, J95.pin1, J101.pin1
  N14: R4.Pin_1, Εξάρτημα2.MOSI, J94.pin1, J102.pin1
  N15: R5.Pin_1, J88.pin1, Εξάρτημα2.CE0, J96.pin1

notes:
  +5V Buck Converter
  +(10V-12V) Buck Converter
  GND
  Max 12V
  Max 12V and 0.3A

custom parts:
  MCP23017 I2C I/O Expander: The MCP23017 uses two i2c pins (these can be shared with other i2c devices), and in exchange gives you 16 general purpose pins. You can set each of 16 pins to be input, output, input with a pullup or open drain. There's even the ability to get an interrupt via an external pin when any of the inputs change so you don't have to keep polling the chip.
  Fan - Ventilador: Ventilador de 2 pines, se encuentra comunmente en computadoras de escritorio
  Adafruit T-Cobbler Plus: The Raspberry Pi has landed on the Maker World like a 40-GPIO pinned, quad-USB ported, credit card sized bomb of DIY joy. And while you can use most of our great Model B accessories by hooking up our downgrade cable, its probably a good time to upgrade your set up and accessorize using all of the 40 pins. That's why we now carry the Assembled Adafruit Pi T-Cobbler Plus - Breakout + Cable for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
