# Fritzing sketch Water Cooling Conection System (saved by Fritzing 0.9.3b)
stripboards: 2

parts:
  F1 = fan_Ventilador
  M1 = DC Motor [part_number="Water Pump"]
  JP15 = M16 [package=1x16_machine-pin-header_lock.004]
  JP16 = M16 [package=1x16_machine-pin-header_lock.004]
  J64 = male pin header, 1 pin [form="♂ (male)"]
  Raspberry_Pi2 = Raspberry Pi B+
  IC2 = MCP23017 I2C I/O Expander [part_number=MCP23S17(IC1)]
  IC3 = L293D [part_number=L293D(IC0) package=THT]
  J65 = male pin header, 1 pin [form="♂ (male)"]
  J66 = male pin header, 1 pin [form="♂ (male)"]
  J67 = male pin header, 1 pin [form="♂ (male)"]
  J68 = male pin header, 1 pin [form="♂ (male)"]
  J69 = male pin header, 1 pin [form="♂ (male)"]
  J70 = male pin header, 1 pin [form="♂ (male)"]
  J71 = male pin header, 1 pin [form="♂ (male)"]
  J72 = male pin header, 1 pin [form="♂ (male)"]
  J73 = male pin header, 1 pin [form="♂ (male)"]
  J74 = male pin header, 1 pin [form="♂ (male)"]
  J75 = male pin header, 1 pin [form="♂ (male)"]
  J76 = male pin header, 1 pin [form="♂ (male)"]
  J77 = male pin header, 1 pin [form="♂ (male)"]
  J78 = male pin header, 1 pin [form="♂ (male)"]
  J79 = male pin header, 1 pin [form="♂ (male)"]
  J80 = male pin header, 1 pin [form="♂ (male)"]
  J81 = male pin header, 1 pin [form="♂ (male)"]
  J82 = male pin header, 1 pin [form="♂ (male)"]
  J83 = male pin header, 1 pin [form="♂ (male)"]
  J84 = male pin header, 1 pin [form="♂ (male)"]
  J85 = male pin header, 1 pin [form="♂ (male)"]

nets:
  N1: F1.connector0, IC3.Out_2_(_Controlled_by_Enable_1_), J72.pin1
  N2: F1.connector1, M1.pin_1, JP15.13, JP16.16, IC3.0V, J68.pin1, J69.pin1, J70.pin1, J71.pin1
  N3: M1.pin_2, IC3.Out_1_(_Controlled_by_Enable_1_), J67.pin1
  N4: JP15.1, IC2.VDD, J75.pin1
  N5: JP15.2, IC2.A0, J85.pin1
  N6: JP15.3, IC3.Enable_1, J65.pin1
  N7: JP15.4, J64.pin1, IC3.+V
  N8: JP15.14, IC2.A2, J83.pin1
  N9: JP15.15, IC2.A1, J84.pin1
  N10: JP15.16, IC2.VSS, J76.pin1
  N11: JP16.1, IC3.+Vmotor, J74.pin1
  N12: Raspberry_Pi2.GPIO10, IC2.SI, J79.pin1
  N13: Raspberry_Pi2.GPIO9, IC2.SO, J80.pin1
  N14: Raspberry_Pi2.GPIO11, IC2.SCK, J78.pin1
  N15: Raspberry_Pi2.GPIO8, IC2.CS, J77.pin1
  N16: IC2.GPA0, IC3.In_1, J66.pin1, J82.pin1
  N17: IC2.GPA1, IC3.In_2, J73.pin1, J81.pin1

notes:
  5V Buck Converter
  8V Buck Converter

custom parts:
  MCP23017 I2C I/O Expander: The MCP23017 uses two i2c pins (these can be shared with other i2c devices), and in exchange gives you 16 general purpose pins. You can set each of 16 pins to be input, output, input with a pullup or open drain. There's even the ability to get an interrupt via an external pin when any of the inputs change so you don't have to keep polling the chip.
