# Fritzing sketch Servo Controller (saved by Fritzing 0.9.3b)

parts:
  J1 = Basic Servo [part_number=MG996R]
  Raspberry_Pi_1 = Raspberry Pi 3 [part_number=RPI-3-V1.2]
  R1 = Resistor [tolerance=±5% resistance=3.3k package="0402 [SMD]"]

nets:
  N1: J1.pulse, R1.Pin_0
  N2: Raspberry_Pi_1.GPIO25, R1.Pin_1

notes:
  The less current possible, just to function properly.
  From Servo Backup Circuit...
  MG996R servo has a running current of 500mA to 900mA @6V and a stall current of 2.5A @ 6V
