# Fritzing sketch BTS7960 Connection System (saved by Fritzing 0.9.3b)
stripboards: 3
perfboards: 2

parts:
  M1 = BTS7960 [part_number=BTS7960(IC0)]
  M2 = BTS7960 [part_number=BTS7960(IC1)]
  M3 = BTS7960 [part_number=BTS7960(IC3)]
  M4 = BTS7960 [part_number=BTS7960(IC2)]
  U1 = 4053 [part_number=74HC4053(IC0) package="DIP (Dual Inline) [THT]"]
  Εξάρτημα1 = 4053 [package="DIP (Dual Inline) [THT]"]  # not connected
  U1_1 = 4053 [package="DIP (Dual Inline) [THT]"]  # not connected
  U1_2 = 4053 [package="DIP (Dual Inline) [THT]"]  # not connected
  U1_3 = 4053 [package="DIP (Dual Inline) [THT]"]  # not connected
  IC1 = MCP23017 I2C I/O Expander [part_number=MCP23S17(IC0)]
  Raspberry_Pi1 = Raspberry Pi B+
  U2 = 4053 [part_number=74HC4053(IC1) package="DIP (Dual Inline) [THT]"]
  U2_3 = 4053 [package="DIP (Dual Inline) [THT]"]  # not connected
  U2_2 = 4053 [package="DIP (Dual Inline) [THT]"]  # not connected
  U2_1 = 4053 [package="DIP (Dual Inline) [THT]"]  # not connected
  Εξάρτημα2 = 4053 [package="DIP (Dual Inline) [THT]"]  # not connected
  JP14 = M16 [package=1x16_machine-pin-header_lock.004]
  JP13 = M16 [package=1x16_machine-pin-header_lock.004]
  JP15 = Header 12 [package=1x12_machine-pin-header_lock.004]
  R1 = Resistor [tolerance=±5% resistance=3.3k package="0402 [SMD]"]
  J8 = male pin header, 1 pin [form="♂ (male)"]
  R2 = Resistor [tolerance=±5% resistance=3.3k package="0402 [SMD]"]
  R3 = Resistor [tolerance=±5% resistance=3.3k package="0402 [SMD]"]  # not connected
  R4 = Resistor [tolerance=±5% resistance=3.3k package="0402 [SMD]"]
  J9 = male pin header, 1 pin [form="♂ (male)"]
  J10 = male pin header, 1 pin [form="♂ (male)"]
  J11 = male pin header, 1 pin [form="♂ (male)"]
  J12 = male pin header, 1 pin [form="♂ (male)"]
  J13 = male pin header, 1 pin [form="♂ (male)"]
  J14 = male pin header, 1 pin [form="♂ (male)"]
  J15 = male pin header, 1 pin [form="♂ (male)"]
  J16 = male pin header, 1 pin [form="♂ (male)"]
  J17 = male pin header, 1 pin [form="♂ (male)"]
  J18 = male pin header, 1 pin [form="♂ (male)"]
  J19 = male pin header, 1 pin [form="♂ (male)"]
  J20 = male pin header, 1 pin [form="♂ (male)"]
  J21 = male pin header, 1 pin [form="♂ (male)"]
  J22 = male pin header, 1 pin [form="♂ (male)"]
  J23 = male pin header, 1 pin [form="♂ (male)"]
  J24 = male pin header, 1 pin [form="♂ (male)"]
  J25 = male pin header, 1 pin [form="♂ (male)"]
  J26 = male pin header, 1 pin [form="♂ (male)"]
  R5 = Resistor [tolerance=±5% resistance=3.3k package="0402 [SMD]"]
  R6 = Resistor [tolerance=±5% resistance=3.3k package="0402 [SMD]"]
  R7 = Resistor [tolerance=±5% resistance=3.3k package="0402 [SMD]"]
  R8 = Resistor [tolerance=±5% resistance=3.3k package="0402 [SMD]"]  # not connected
  J27 = male pin header, 1 pin [form="♂ (male)"]
  J28 = male pin header, 1 pin [form="♂ (male)"]
  J29 = male pin header, 1 pin [form="♂ (male)"]
  J30 = male pin header, 1 pin [form="♂ (male)"]
  J31 = male pin header, 1 pin [form="♂ (male)"]
  J32 = male pin header, 1 pin [form="♂ (male)"]
  J33 = male pin header, 1 pin [form="♂ (male)"]
  J34 = male pin header, 1 pin [form="♂ (male)"]
  J35 = male pin header, 1 pin [form="♂ (male)"]
  J36 = male pin header, 1 pin [form="♂ (male)"]
  J37 = male pin header, 1 pin [form="♂ (male)"]
  J38 = male pin header, 1 pin [form="♂ (male)"]
  J39 = male pin header, 1 pin [form="♂ (male)"]
  J40 = male pin header, 1 pin [form="♂ (male)"]
  J41 = male pin header, 1 pin [form="♂ (male)"]
  J42 = male pin header, 1 pin [form="♂ (male)"]
  J43 = male pin header, 1 pin [form="♂ (male)"]
  J44 = male pin header, 1 pin [form="♂ (male)"]
  J45 = male pin header, 1 pin [form="♂ (male)"]
  J46 = male pin header, 1 pin [form="♂ (male)"]
  J47 = male pin header, 1 pin [form="♂ (male)"]
  J48 = male pin header, 1 pin [form="♂ (male)"]
  J49 = male pin header, 1 pin [form="♂ (male)"]
  J50 = male pin header, 1 pin [form="♂ (male)"]
  J51 = male pin header, 1 pin [form="♂ (male)"]
  J52 = male pin header, 1 pin [form="♂ (male)"]
  J53 = male pin header, 1 pin [form="♂ (male)"]
  J54 = male pin header, 1 pin [form="♂ (male)"]
  J55 = male pin header, 1 pin [form="♂ (male)"]
  J56 = male pin header, 1 pin [form="♂ (male)"]
  J57 = male pin header, 1 pin [form="♂ (male)"]
  J58 = male pin header, 1 pin [form="♂ (male)"]
  J59 = male pin header, 1 pin [form="♂ (male)"]
  J60 = male pin header, 1 pin [form="♂ (male)"]
  J61 = male pin header, 1 pin [form="♂ (male)"]
  J62 = male pin header, 1 pin [form="♂ (male)"]
  J63 = male pin header, 1 pin [form="♂ (male)"]
  J64 = male pin header, 1 pin [form="♂ (male)"]
  J65 = male pin header, 1 pin [form="♂ (male)"]
  J66 = male pin header, 1 pin [form="♂ (male)"]
  J67 = male pin header, 1 pin [form="♂ (male)"]
  J68 = male pin header, 1 pin [form="♂ (male)"]
  J69 = male pin header, 1 pin [form="♂ (male)"]
  J70 = male pin header, 1 pin [form="♂ (male)"]
  J71 = male pin header, 1 pin [form="♂ (male)"]
  J72 = male pin header, 1 pin [form="♂ (male)"]
  J73 = male pin header, 1 pin [form="♂ (male)"]
  J74 = male pin header, 1 pin [form="♂ (male)"]
  J75 = male pin header, 1 pin [form="♂ (male)"]
  J76 = male pin header, 1 pin [form="♂ (male)"]
  J77 = male pin header, 1 pin [form="♂ (male)"]
  J78 = male pin header, 1 pin [form="♂ (male)"]
  J79 = male pin header, 1 pin [form="♂ (male)"]
  J80 = male pin header, 1 pin [form="♂ (male)"]

nets:
  N1: M1.pin1, U1.connector11, R1.Pin_1, J9.pin1, J29.pin1, J31.pin1
  N2: M1.pin2, U1.connector12, J11.pin1, J17.pin1, J18.pin1
  N3: M1.pin3, M1.pin4, M3.pin3, M3.pin4, IC1.GPA3, IC1.GPB4, J47.pin1, J48.pin1, J56.pin1, J57.pin1
  N4: M1.pin7, JP14.1
  N5: M1.pin8, JP13.5
  N6: M1.pin11, JP15.2
  N7: M1.pin12, JP15.10
  N8: M2.pin1, U1.connector1, R2.Pin_1, R4.Pin_1, J13.pin1, J37.pin1, J38.pin1
  N9: M2.pin2, U1.connector0, J12.pin1, J35.pin1, J36.pin1
  N10: M2.pin3, M2.pin4, M4.pin3, M4.pin4, IC1.GPA4, IC1.GPB3, J49.pin1, J50.pin1, J54.pin1, J55.pin1
  N11: M2.pin7, JP14.2
  N12: M2.pin8, JP13.4
  N13: M2.pin11, JP15.1
  N14: M2.pin12, JP15.9
  N15: M3.pin1, U2.connector1, J25.pin1, J75.pin1, J77.pin1
  N16: M3.pin2, U2.connector0, J19.pin1, R7.Pin_0, J74.pin1, J76.pin1
  N17: M3.pin7, JP14.7
  N18: M3.pin8, JP13.3
  N19: M3.pin11, JP15.4
  N20: M3.pin12, JP15.12
  N21: M4.pin1, U2.connector11, J26.pin1, R6.Pin_0, J70.pin1, J71.pin1
  N22: M4.pin2, U2.connector12, J23.pin1, R5.Pin_0, J68.pin1, J69.pin1
  N23: M4.pin7, JP14.3
  N24: M4.pin8, JP13.16
  N25: M4.pin11, JP15.3
  N26: M4.pin12, JP15.11
  N27: U1.connector5, JP13.8, J39.pin1
  N28: U1.connector6, JP13.6, J40.pin1
  N29: U1.connector7, JP13.7, J41.pin1
  N30: U1.connector8, IC1.GPA2, IC1.GPB5, J34.pin1, J58.pin1
  N31: U1.connector9, IC1.GPA1, IC1.GPB6, J33.pin1, J59.pin1
  N32: U1.connector10, IC1.GPA0, IC1.GPB7, J32.pin1, J60.pin1
  N33: U1.connector13, Raspberry_Pi1.GPIO13, J30.pin1
  N34: U1.connector14, Raspberry_Pi1.GPIO19, J28.pin1
  N35: U1.connector15, JP14.4, J27.pin1
  N36: IC1.A0, IC1.SO, Raspberry_Pi1.GPIO9, JP13.12, J8.pin1, J63.pin1
  N37: IC1.A1, IC1.SI, Raspberry_Pi1.GPIO10, JP13.11, J42.pin1, J62.pin1
  N38: IC1.A2, IC1.SCK, Raspberry_Pi1.GPIO11, JP13.10, J43.pin1, J61.pin1
  N39: IC1.RESET, IC1.CS, Raspberry_Pi1.GPIO8, J44.pin1
  N40: IC1.INTB, IC1.VSS, JP13.9, J45.pin1
  N41: IC1.INTA, IC1.VDD, JP14.5, J46.pin1
  N42: IC1.GPA5, IC1.GPB2, U2.connector8, J51.pin1, J73.pin1
  N43: IC1.GPA6, IC1.GPB1, U2.connector9, J52.pin1, J72.pin1
  N44: IC1.GPA7, IC1.GPB0, U2.connector10, J53.pin1, J66.pin1
  N45: Raspberry_Pi1.GND, JP14.10
  N46: Raspberry_Pi1.GPIO12, U2.connector14, J65.pin1
  N47: Raspberry_Pi1.GPIO18, U2.connector13, J67.pin1
  N48: U2.connector5, JP13.13, J78.pin1
  N49: U2.connector6, JP13.14, J79.pin1
  N50: U2.connector7, JP13.15, J80.pin1
  N51: U2.connector15, JP14.6, J64.pin1
  N52: JP14.11, R1.Pin_0, J10.pin1
  N53: JP14.12, R2.Pin_0, J14.pin1
  N54: JP14.13, J16.pin1
  N55: JP14.14, R4.Pin_0, J15.pin1
  N56: JP14.15, J24.pin1, R5.Pin_1
  N57: JP14.16, J21.pin1
  N58: JP13.1, J22.pin1
  N59: JP13.2, J20.pin1, R6.Pin_1, R7.Pin_1

notes:
  24V Power Source
  5V Buck Converter
  OVERAL TODO
  The mirroring left-right motors motion will be handle in source code at functions like moveForwardFrontLeftMotor(), moveBackwardFrontLeftMotor(), etc for the other 3 motors.

custom parts:
  BTS7960: BTS7960 43A Peak Power H-Bridge PWM Motor Driver
  4053: A 4053 three element single throw double pole analog switch in schematic subpart format.
  4053: A 4053 three element single throw double pole analog switch in schematic subpart format.
  4053: A 4053 three element single throw double pole analog switch in schematic subpart format.
  4053: A 4053 three element single throw double pole analog switch in schematic subpart format.
  4053: A 4053 three element single throw double pole analog switch in schematic subpart format.
  MCP23017 I2C I/O Expander: The MCP23017 uses two i2c pins (these can be shared with other i2c devices), and in exchange gives you 16 general purpose pins. You can set each of 16 pins to be input, output, input with a pullup or open drain. There's even the ability to get an interrupt via an external pin when any of the inputs change so you don't have to keep polling the chip.
